# Fritzing sketch Flashing_Light_Breadboard_1 (saved by Fritzing 1.0.0rc)
breadboards: 1

parts:
  LED1 = LED - 5mm [color="Red (633nm)" current=0.030A package="5 mm [THT]"]
  R1 = Resistor [tolerance=±5% power=0.25W resistance=220 package=THT]
  Unda_Make1 = Unda.Make

nets:
  N1: LED1.cathode, Unda_Make1.GND
  N2: LED1.anode, R1.Pin_1
  N3: R1.Pin_0, Unda_Make1.D2

custom parts:
  Unda.Make: Unda.Make is a digital Electonics platform for teaching STEM in a simple and fun way. It supports inbuilt projects as well as user downloaded projects.
