# Fritzing sketch Ambulance_Siren Breadboard (saved by Fritzing 1.0.0rc)
breadboards: 1

parts:
  Unda_Make1 = Unda.Make
  J1 = Buzzer
  R4 = Resistor [tolerance=±5% power=0.25W resistance=220 package=THT]
  S1 = Pushbutton [package="[SMD]"]
  R2 = Resistor [tolerance=±5% power=0.25W resistance=220 package=THT]
  R3 = Resistor [tolerance=±5% power=0.25W resistance=220 package=THT]
  R1 = Resistor [tolerance=±5% power=0.25W resistance=220 package=THT]
  LED1 = RGB LED - (4 legs) [color="Red (633nm)" current=0.030A package="5 mm [THT]"]  # not connected

nets:
  N1: Unda_Make1.D2, R1.Pin_1
  N2: Unda_Make1.D3, R3.Pin_0
  N3: Unda_Make1.D6, R2.Pin_0
  N4: Unda_Make1.D10, J1.pin2
  N5: Unda_Make1.D13, R4.Pin_1, S1.Pin_1, S1.Pin_2
  N6: Unda_Make1.GND, J1.pin1, R4.Pin_0
  N7: Unda_Make1.5V, Unda_Make1.RST, S1.Pin_3, S1.Pin_4

custom parts:
  Unda.Make: Unda.Make is a digital Electonics platform for teaching STEM in a simple and fun way. It supports inbuilt projects as well as user downloaded projects.
  Buzzer: Piezo
