# Fritzing sketch Fan_Breadboard (saved by Fritzing 1.0.0rc)
breadboards: 1

parts:
  Unda_Make1 = Unda.Make
  M1 = DC Motor
  R3 = Resistor [tolerance=±5% power=0.25W resistance=220 package=THT]
  S2 = Pushbutton [package="[THT]"]

nets:
  N1: Unda_Make1.D2, R3.Pin_0, S2.Pin_1, S2.Pin_2
  N2: Unda_Make1.D10, M1.pin_2
  N3: Unda_Make1.5V, R3.Pin_1, S2.Pin_3, S2.Pin_4
  N4: Unda_Make1.GND, M1.pin_1

custom parts:
  Unda.Make: Unda.Make is a digital Electonics platform for teaching STEM in a simple and fun way. It supports inbuilt projects as well as user downloaded projects.
  DC Motor: 5V Micro DC Motor
