# Fritzing sketch KEYBOARD_BREADBOARD (saved by Fritzing 1.0.0rc)
breadboards: 1

parts:
  Unda_Make1 = Unda.Make
  S1 = Pushbutton [package="[SMD]"]
  S2 = Pushbutton [package="[SMD]"]
  S3 = Pushbutton [package="[SMD]"]
  S4 = Pushbutton [package="[SMD]"]
  R9 = Resistor [tolerance=±5% power=0.25W resistance=220 package=THT]
  R10 = Resistor [tolerance=±5% power=0.25W resistance=220 package=THT]
  R11 = Resistor [tolerance=±5% power=0.25W resistance=220 package=THT]
  R12 = Resistor [tolerance=±5% power=0.25W resistance=220 package=THT]

nets:
  N1: Unda_Make1.D7, S3.Pin_3, S3.Pin_4
  N2: Unda_Make1.D8, S4.Pin_3, S4.Pin_4
  N3: Unda_Make1.D9, S2.Pin_3, S2.Pin_4
  N4: Unda_Make1.D10, S1.Pin_3, S1.Pin_4
  N5: Unda_Make1.5V, Unda_Make1.RST, S1.Pin_1, S1.Pin_2, S2.Pin_1, S2.Pin_2, S3.Pin_1, S3.Pin_2, S4.Pin_1, S4.Pin_2, R9.Pin_0, R10.Pin_0, R11.Pin_0, R12.Pin_0
  N6: Unda_Make1.GND, R9.Pin_1, R10.Pin_1, R11.Pin_1, R12.Pin_1

custom parts:
  Unda.Make: Unda.Make is a digital Electonics platform for teaching STEM in a simple and fun way. It supports inbuilt projects as well as user downloaded projects.
