# Fritzing sketch Level_Meter_Breadboard (saved by Fritzing 1.0.0rc)
breadboards: 1

parts:
  Unda_Make1 = Unda.Make
  R2 = Rotary Potentiometer (Small) [maximum_resistance=10kΩ knob_status=50% power=0.5W package=THT]
  R1 = Resistor [tolerance=±5% power=0.25W resistance=220 package=THT]
  R3 = Resistor [tolerance=±5% power=0.25W resistance=220 package=THT]
  LED1 = LED - 5mm [color="Green (570nm)" current=0.030A package="5 mm [THT]"]
  LED2 = LED - 5mm [color="Orange (620nm)" current=0.030A package="5 mm [THT]"]
  LED3 = LED - 5mm [color="Red (633nm)" current=0.030A package="5 mm [THT]"]
  R4 = Resistor [tolerance=±5% power=0.25W resistance=220 package=THT]

nets:
  N1: Unda_Make1.D4, R1.Pin_1
  N2: Unda_Make1.D5, R3.Pin_1
  N3: Unda_Make1.D6, R4.Pin_1
  N4: Unda_Make1.A0, R2.wiper
  N5: Unda_Make1.5V, Unda_Make1.RST, R2.leg2
  N6: Unda_Make1.GND, R2.leg1, LED1.cathode, LED2.cathode, LED3.cathode
  N7: R1.Pin_0, LED1.anode
  N8: R3.Pin_0, LED2.anode
  N9: LED3.anode, R4.Pin_0

notes:
  +
  -

custom parts:
  Unda.Make: Unda.Make is a digital Electonics platform for teaching STEM in a simple and fun way. It supports inbuilt projects as well as user downloaded projects.
