# Fritzing sketch Light_Dimming Breadboar (saved by Fritzing 1.0.0rc)
breadboards: 1

parts:
  Unda_Make1 = Unda.Make
  R1 = Rotary Potentiometer (Small) [maximum_resistance=10kΩ knob_status=50% power=0.5W package=THT]
  R2 = Resistor [tolerance=±5% power=0.25W resistance=220 package=THT]
  LED1 = LED - 5mm [color="Red (633nm)" current=0.030A package="5 mm [THT]"]

nets:
  N1: Unda_Make1.D3, R2.Pin_1
  N2: Unda_Make1.A7, R1.wiper
  N3: Unda_Make1.GND, R1.leg1, LED1.cathode
  N4: Unda_Make1.5V, R1.leg2
  N5: R2.Pin_0, LED1.anode

custom parts:
  Unda.Make: Unda.Make is a digital Electonics platform for teaching STEM in a simple and fun way. It supports inbuilt projects as well as user downloaded projects.
