# Fritzing sketch Notification_Light_breadboard (saved by Fritzing 1.0.0rc)
breadboards: 1

parts:
  Unda_Make1 = Unda.Make
  S2 = Pushbutton [package="[THT]"]
  R4 = Resistor [tolerance=±5% power=0.25W resistance=220 package=THT]
  LED1 = RGB LED (com. cathode, rbg) [color="Red (633nm)" current=0.030A package="5 mm [THT]"]
  R1 = Resistor [tolerance=±5% power=0.25W resistance=220 package=THT]
  R3 = Resistor [tolerance=±5% power=0.25W resistance=220 package=THT]
  R2 = Resistor [tolerance=±5% power=0.25W resistance=220 package=THT]

nets:
  N1: Unda_Make1.D4, R3.Pin_0
  N2: Unda_Make1.D6, R2.Pin_0
  N3: Unda_Make1.D10, S2.Pin_1, S2.Pin_2, R4.Pin_1
  N4: Unda_Make1.GND, R4.Pin_0, LED1.common_cathode
  N5: S2.Pin_3, S2.Pin_4
  N6: LED1.red_anode, R1.Pin_1
  N7: LED1.blue_anode, R3.Pin_1
  N8: LED1.green_anode, R2.Pin_1

custom parts:
  Unda.Make: Unda.Make is a digital Electonics platform for teaching STEM in a simple and fun way. It supports inbuilt projects as well as user downloaded projects.
