# Fritzing sketch Smart_Bulb_Breadboard (saved by Fritzing 1.0.0rc)
breadboards: 1

parts:
  LED1 = RGB LED (com. cathode, rbg) [color="Red (633nm)" current=0.030A package="5 mm [THT]"]
  Unda_Make1 = Unda.Make
  R1 = Resistor [tolerance=±5% power=0.25W resistance=220 package=THT]
  R2 = Resistor [tolerance=±5% power=0.25W resistance=220 package=THT]
  R3 = Resistor [tolerance=±5% power=0.25W resistance=220 package=THT]

nets:
  N1: LED1.red_anode, R1.Pin_0
  N2: LED1.common_cathode, Unda_Make1.GND
  N3: LED1.blue_anode, R3.Pin_1
  N4: LED1.green_anode, R2.Pin_1
  N5: Unda_Make1.D2, R1.Pin_1
  N6: Unda_Make1.D4, R3.Pin_0
  N7: Unda_Make1.D6, R2.Pin_0

custom parts:
  Unda.Make: Unda.Make is a digital Electonics platform for teaching STEM in a simple and fun way. It supports inbuilt projects as well as user downloaded projects.
