# Fritzing sketch Smart_Home_Breadboard (saved by Fritzing 1.0.0rc)
breadboards: 1

parts:
  Unda_Make1 = Unda.Make
  R2 = Resistor [tolerance=±5% resistance=220 package="2512 [SMD]"]
  R1 = Photocell (LDR) [power=0.25W dark_resistance_@0.01lx=300kΩ light_resistance_@100lx=400Ω luminance=10lx package=THT]
  T1 = TMP36 Temperature Sensor [package="TO92 [THT]"]

nets:
  N1: Unda_Make1.A0, R2.Pin_0, R1.pin_1
  N2: Unda_Make1.A6, Unda_Make1.5V#47, T1.Vout
  N3: Unda_Make1.5V#46, R1.pin_0, T1.+Vs
  GND: Unda_Make1.GND, R2.Pin_1, T1.GND

custom parts:
  Unda.Make: Unda.Make is a digital Electonics platform for teaching STEM in a simple and fun way. It supports inbuilt projects as well as user downloaded projects.
