# Fritzing sketch SPEEDOMETER_BREADBOARD (saved by Fritzing 1.0.0rc)
breadboards: 1

parts:
  Unda_Make1 = Unda.Make
  M1 = DC Motor
  R4 = Rotary Potentiometer (Small) [maximum_resistance=10kΩ knob_status=50% power=0.5W package=THT]

nets:
  N1: Unda_Make1.D10, M1.pin_2
  N2: Unda_Make1.A4, R4.wiper
  N3: Unda_Make1.GND, M1.pin_1, R4.leg1
  N4: Unda_Make1.5V, R4.leg2

custom parts:
  Unda.Make: Unda.Make is a digital Electonics platform for teaching STEM in a simple and fun way. It supports inbuilt projects as well as user downloaded projects.
  DC Motor: 5V Micro DC Motor
