# Fritzing sketch stop_watch_breadboard (saved by Fritzing 1.0.0rc)
breadboards: 1

parts:
  Unda_Make1 = Unda.Make
  S1 = Momentary Switch [package=ksa_sealed_tac_switch]
  S2 = Momentary Switch [package=ksa_sealed_tac_switch]
  R6 = Resistor [tolerance=±5% power=0.25W resistance=220 package=THT]
  R8 = Resistor [tolerance=±5% power=0.25W resistance=220 package=THT]

nets:
  N1: Unda_Make1.D12, S2.1
  N2: Unda_Make1.D13, S1.1
  N3: Unda_Make1.5V, Unda_Make1.RST, S1.3, S2.3
  N4: Unda_Make1.GND, R6.Pin_1, R8.Pin_1
  N5: S1.2, R8.Pin_0
  N6: S2.2, R6.Pin_0

custom parts:
  Unda.Make: Unda.Make is a digital Electonics platform for teaching STEM in a simple and fun way. It supports inbuilt projects as well as user downloaded projects.
