# Fritzing sketch Timer_breadboard (saved by Fritzing 1.0.0rc)
breadboards: 1

parts:
  Unda_Make1 = Unda.Make
  R2 = Resistor [tolerance=±5% resistance=220 package="0402 [SMD]"]
  R3 = Resistor [tolerance=±5% resistance=220 package="0402 [SMD]"]
  S2 = Pushbutton [package="[THT]"]
  S1 = Pushbutton [package="[THT]"]
  J1 = Buzzer

nets:
  N1: Unda_Make1.D2, J1.pin1
  N2: Unda_Make1.D12, R2.Pin_0, S1.Pin_1, S1.Pin_2
  N3: Unda_Make1.D13, R3.Pin_1, S2.Pin_1, S2.Pin_2
  N4: Unda_Make1.5V, S2.Pin_3, S2.Pin_4, S1.Pin_3, S1.Pin_4
  N5: Unda_Make1.GND, R2.Pin_1, R3.Pin_0, J1.pin2

custom parts:
  Unda.Make: Unda.Make is a digital Electonics platform for teaching STEM in a simple and fun way. It supports inbuilt projects as well as user downloaded projects.
  Buzzer: Piezo
