# Fritzing sketch Traffic_lights_Breadboard (saved by Fritzing 1.0.0rc)
breadboards: 1

parts:
  LED1 = LED - 5mm [color="Green (570nm)" current=0.030A package="5 mm [THT]"]
  LED2 = LED - 5mm [color="Orange (620nm)" current=0.030A package="5 mm [THT]"]
  LED3 = LED - 5mm [color="Red (660nm)" current=0.030A package="5 mm [THT]"]
  R1 = Resistor [tolerance=±5% power=0.25W resistance=220 package=THT]
  R2 = Resistor [tolerance=±5% power=0.25W resistance=220 package=THT]
  R3 = Resistor [tolerance=±5% power=0.25W resistance=220 package=THT]
  Unda_Make1 = Unda.Make

nets:
  N1: LED1.cathode, LED2.cathode, LED3.cathode, Unda_Make1.GND
  N2: LED1.anode, R1.Pin_1
  N3: LED2.anode, R2.Pin_1
  N4: LED3.anode, R3.Pin_1
  N5: R1.Pin_0, Unda_Make1.D2
  N6: R2.Pin_0, Unda_Make1.D5
  N7: R3.Pin_0, Unda_Make1.D9

custom parts:
  Unda.Make: Unda.Make is a digital Electonics platform for teaching STEM in a simple and fun way. It supports inbuilt projects as well as user downloaded projects.
