# Fritzing sketch Volume_Control_Breadboard (saved by Fritzing 1.0.0rc)
breadboards: 1

parts:
  Unda_Make1 = Unda.Make
  R3 = Rotary Potentiometer (Small) [maximum_resistance=10kΩ knob_status=50% power=0.5W package=THT]
  J1 = Buzzer

nets:
  N1: Unda_Make1.D11, J1.pin2
  N2: Unda_Make1.A3, R3.wiper
  N3: Unda_Make1.GND, J1.pin1
  N4: Unda_Make1.5V, R3.leg2

custom parts:
  Unda.Make: Unda.Make is a digital Electonics platform for teaching STEM in a simple and fun way. It supports inbuilt projects as well as user downloaded projects.
  Buzzer: Piezo
