# Fritzing sketch Light_Switch_breadboard (saved by Fritzing 1.0.0rc)
breadboards: 1

parts:
  Unda_Make1 = Unda.Make
  S2 = Pushbutton [package="[THT]"]
  R4 = Resistor [tolerance=±5% power=0.25W resistance=220 package=THT]
  R1 = Resistor [tolerance=±5% power=0.25W resistance=220 package=THT]
  LED1 = LED - 5mm [color="Red (660nm)" current=0.030A package="5 mm [THT]"]

nets:
  N1: Unda_Make1.D4, R1.Pin_0
  N2: Unda_Make1.D10, S2.Pin_1, S2.Pin_2, R4.Pin_1
  N3: Unda_Make1.5V, S2.Pin_3, S2.Pin_4
  N4: R4.Pin_0, LED1.cathode
  N5: R1.Pin_1, LED1.anode

custom parts:
  Unda.Make: Unda.Make is a digital Electonics platform for teaching STEM in a simple and fun way. It supports inbuilt projects as well as user downloaded projects.
