# Fritzing sketch Oven_Control Breadboard (saved by Fritzing 1.0.0rc)
breadboards: 1

parts:
  Unda_Make1 = Unda.Make
  T1 = TMP36 Temperature Sensor [package="TO92 [THT]"]
  R2 = Resistor [tolerance=±5% power=0.25W resistance=220 package=THT]
  LED6 = LED - 5mm [color="Green (570nm)" current=0.030A package="5 mm [THT]"]
  LED5 = LED - 5mm [color="Red (635nm)" current=0.030A package="5 mm [THT]"]
  R1 = Resistor [tolerance=±5% power=0.25W resistance=220 package=THT]

nets:
  N1: Unda_Make1.D2, R1.Pin_0
  N2: Unda_Make1.D3, R2.Pin_1
  N3: Unda_Make1.A1, T1.Vout
  N4: Unda_Make1.5V, T1.+Vs
  N5: R2.Pin_0, LED6.anode
  N6: LED5.anode, R1.Pin_1

notes:
  -
  +

custom parts:
  Unda.Make: Unda.Make is a digital Electonics platform for teaching STEM in a simple and fun way. It supports inbuilt projects as well as user downloaded projects.
