# Fritzing sketch Running_lights_breadboard (saved by Fritzing 1.0.0rc)
breadboards: 1

parts:
  R1 = Resistor [tolerance=±5% power=0.25W resistance=220 package=THT]
  LED2 = LED - 5mm [color="Orange (605nm)" current=0.030A package="5 mm [THT]"]
  R2 = Resistor [tolerance=±5% power=0.25W resistance=220 package=THT]
  LED3 = LED - 5mm [color="Blue (525nm)" current=0.030A package="5 mm [THT]"]
  LED4 = LED - 5mm [color="Yellow (595nm)" current=0.030A package="5 mm [THT]"]
  LED5 = LED - 5mm [color="Red (660nm)" current=0.030A package="5 mm [THT]"]
  R3 = Resistor [tolerance=±5% power=0.25W resistance=220 package=THT]
  R4 = Resistor [tolerance=±5% power=0.25W resistance=220 package=THT]
  R5 = Resistor [tolerance=±5% power=0.25W resistance=220 package=THT]
  LED6 = LED - 5mm [color="Green (570nm)" current=0.030A package="5 mm [THT]"]
  Unda_Make1 = Unda.Make

nets:
  N1: R1.Pin_0, LED6.anode
  N2: R1.Pin_1, Unda_Make1.D3
  N3: LED2.cathode, LED3.cathode, LED4.cathode, LED5.cathode, LED6.cathode, Unda_Make1.GND
  N4: LED2.anode, R2.Pin_1
  N5: R2.Pin_0, Unda_Make1.D5
  N6: LED3.anode, R3.Pin_1
  N7: LED4.anode, R4.Pin_1
  N8: LED5.anode, R5.Pin_1
  N9: R3.Pin_0, Unda_Make1.D6
  N10: R4.Pin_0, Unda_Make1.D10
  N11: R5.Pin_0, Unda_Make1.D11

custom parts:
  Unda.Make: Unda.Make is a digital Electonics platform for teaching STEM in a simple and fun way. It supports inbuilt projects as well as user downloaded projects.
