# Fritzing sketch Street_Lights_Breadboard (saved by Fritzing 1.0.0rc)
breadboards: 1

parts:
  Unda_Make2 = Unda.Make
  R3 = Resistor [tolerance=±5% power=0.25W resistance=10k package=THT]
  R2 = Photocell (LDR) [power=0.25W dark_resistance_@0.01lx=300kΩ light_resistance_@100lx=400Ω luminance=10lx package=THT]
  R1 = Resistor [tolerance=±5% power=0.25W resistance=220 package=THT]
  LED1 = LED - 5mm [color="Red (633nm)" current=0.030A package="5 mm [THT]"]

nets:
  N1: Unda_Make2.D2, R1.Pin_0
  N2: Unda_Make2.A0, R3.Pin_0
  N3: Unda_Make2.GND, R2.pin_0, LED1.cathode
  N4: R3.Pin_1, R2.pin_1
  N5: R1.Pin_1, LED1.anode

notes:
  -
  +

custom parts:
  Unda.Make: Unda.Make is a digital Electonics platform for teaching STEM in a simple and fun way. It supports inbuilt projects as well as user downloaded projects.
