# Fritzing sketch Thermometer_breadboard (saved by Fritzing 1.0.0rc)
breadboards: 1

parts:
  U1 = TMP36 [package=to-92]
  Unda_Make1 = Unda.Make

nets:
  VCC: U1.VCC, Unda_Make1.5V, Unda_Make1.RST
  N1: U1.VOUT, Unda_Make1.A5
  GND: U1.GND, Unda_Make1.GND

custom parts:
  Unda.Make: Unda.Make is a digital Electonics platform for teaching STEM in a simple and fun way. It supports inbuilt projects as well as user downloaded projects.
